// Logisim project Logisim CPU starter.circ as structural Verilog: 3 circuits, main circuit CPU main
module CPU_main (
);

  wire and_1_out, button_1_out, Clock_out, Instruction_Decoder_branch_always, Instruction_Decoder_halt,
       Instruction_Decoder_use_immediate, Instruction_Decoder_write_acc, Instruction_Decoder_write_memory,
       not_1_out;
  wire [3:0] Instruction_Decoder_alu_operation;
  wire [7:0] ACC_q, adder_1_out, ALU_alu_out_to_acc, Instruction_Decoder_address_or_immediate,
       multiplexer_1_out, multiplexer_2_out, PC_q, ram_2_data;
  wire [15:0] ram_1_data;

  Button button_1 (.out(button_1_out));
  Clock Clock (.out(Clock_out));
  Adder adder_1 (.a(PC_q), .b(8'h1), .out(adder_1_out));  // open: cin, cout
  Multiplexer #(.width(8)) multiplexer_1 (
    .in0(adder_1_out), .in1(Instruction_Decoder_address_or_immediate), .out(multiplexer_1_out),
    .sel(Instruction_Decoder_branch_always));  // open: en
  Register PC (.D(multiplexer_1_out), .en(1'b1), .Q(PC_q), .clk(and_1_out), .clr(button_1_out));
  RAM #(.dataWidth(16)) ram_1 (.addr(PC_q), .data(ram_1_data), .clk(and_1_out), .clr(button_1_out));  // open: sel, ld
  Instruction_Decoding_Unit Instruction_Decoder (
    .Instruction(ram_1_data), .Address_or_Immediate(Instruction_Decoder_address_or_immediate),
    .Write_Memory(Instruction_Decoder_write_memory), .Use_Immediate(Instruction_Decoder_use_immediate),
    .ALU_Operation(Instruction_Decoder_alu_operation), .Write_ACC(Instruction_Decoder_write_acc),
    .Branch_always(Instruction_Decoder_branch_always), .Halt(Instruction_Decoder_halt));  // open: Branch_NE_zero
  not not_1 (not_1_out, Instruction_Decoder_halt);
  and and_1 (and_1_out, Clock_out, not_1_out);
  RAM #(.bus("separate")) ram_2 (
    .addr(Instruction_Decoder_address_or_immediate), .din(ACC_q), .data(ram_2_data),
    .str(Instruction_Decoder_write_memory), .clk(and_1_out), .clr(button_1_out));  // open: sel, ld
  Multiplexer #(.width(8)) multiplexer_2 (
    .in0(ram_2_data), .in1(Instruction_Decoder_address_or_immediate), .out(multiplexer_2_out),
    .sel(Instruction_Decoder_use_immediate));  // open: en
  ALU ALU (
    .ACC_to_ALU(ACC_q), .Inp_to_ALU(multiplexer_2_out), .ALU_Operation(Instruction_Decoder_alu_operation),
    .ALU_out_to_ACC(ALU_alu_out_to_acc));  // open: Not_Equal_Zero
  Register ACC (
    .D(ALU_alu_out_to_acc), .en(Instruction_Decoder_write_acc), .Q(ACC_q), .clk(and_1_out), .clr(button_1_out));

  // Notes on the sheet:
  //   Add 1
  //   Reset
  //   Student id: 21441545
  //   Program memory
  //   Data memory
  //   Output from data memory
  //   SELECT
  //   Output from ACC
endmodule

module ALU (
  input  [7:0] ACC_to_ALU,
  input  [7:0] Inp_to_ALU,
  input  [3:0] ALU_Operation,
  output [7:0] ALU_out_to_ACC,
  output Not_Equal_Zero
);

  wire [7:0] adder_1_out, multiplier_1_out, not_1_out, xor_1_out;

  Adder adder_1 (.a(ACC_to_ALU), .b(Inp_to_ALU), .out(adder_1_out));  // open: cin, cout
  assign xor_1_out = ACC_to_ALU ^ Inp_to_ALU;  // XOR_Gate xor_1, 8 bits wide
  Multiplier multiplier_1 (.a(ACC_to_ALU), .b(Inp_to_ALU), .out(multiplier_1_out));  // open: cin, cout
  assign not_1_out = ~ACC_to_ALU;  // NOT_Gate not_1, 8 bits wide
  Comparator #(.width(1)) comparator_1 (.a(1'b1), .eq(Not_Equal_Zero));  // open: b, gt, lt
  Multiplexer #(.select(4), .width(8)) multiplexer_1 (
    .in0(Inp_to_ALU), .in1(adder_1_out), .in2(xor_1_out), .in3(multiplier_1_out), .in4(not_1_out),
    .out(ALU_out_to_ACC), .sel(ALU_Operation));  // open: in5, in6, in7, in8, in9, in10, in11, in12, in13, in14, in15, en
endmodule

module Instruction_Decoding_Unit (
  input  [15:0] Instruction,
  output [7:0] Address_or_Immediate,
  output Write_Memory,
  output Use_Immediate,
  output [3:0] ALU_Operation,
  output Write_ACC,
  output Branch_always,
  output Branch_NE_zero,
  output Halt
);

  wire decoder_1_out2;

  Decoder #(.select(4)) decoder_1 (
    .out1(Use_Immediate), .out2(decoder_1_out2), .out3(Write_Memory), .out4(Branch_always),
    .out5(Branch_NE_zero), .out15(Halt), .sel(Instruction[15:12]));  // open: out0, out6, out7, out8, out9, out10, out11, out12, out13, out14, en
  or or_1 (Write_ACC, Use_Immediate, decoder_1_out2);

  assign Address_or_Immediate = Instruction[7:0];
  assign ALU_Operation = Instruction[11:8];
endmodule
